# Fritzing sketch Paper_Piano (saved by Fritzing 0.9.2b)
breadboards: 1

parts:
  Raspberry_Pi1 = Raspberry Pi 2
  Q1 = NPN-Transistor [package="TO92 [THT]"]
  Q2 = NPN-Transistor [package="TO92 [THT]"]
  Q3 = PNP-Transistor [package="TO92 [THT]"]
  Q4 = PNP-Transistor [package="TO92 [THT]"]
  LED1 = RGB LED (com. cathode, rgb) [package="5 mm [THT]"]
  S1 = Pushbutton [package="[THT]"]
  S2 = Pushbutton [package="[THT]"]

nets:
  N1: Raspberry_Pi1.3v3, Q1.C, Q2.C, Q3.E, Q4.E
  N2: Raspberry_Pi1.GPIO19, S1.Pin_3, S1.Pin_4
  N3: Raspberry_Pi1.GPIO26, S2.Pin_3, S2.Pin_4
  N4: Raspberry_Pi1.GND, LED1.common_cathode, S1.Pin_1, S1.Pin_2, S2.Pin_1, S2.Pin_2
  N5: Raspberry_Pi1.GPIO21, LED1.blue_anode
  N6: Raspberry_Pi1.GPIO20, LED1.green_anode
  N7: Raspberry_Pi1.GPIO16, LED1.red_anode
  N8: Raspberry_Pi1.GPIO25, Q4.C
  N9: Raspberry_Pi1.GPIO24, Q3.C
  N10: Raspberry_Pi1.GPIO23, Q2.E
  N11: Raspberry_Pi1.GPIO18, Q1.E

notes:
  3v3
  GND
  Emitter
  Collector
  GPIO18 (Pin 12)
  GPIO23 (Pin 16)
  GPIO24 (Pin 18)
  GPIO25 (Pin 22)
  GPIO19 (Pin 35)
  GPIO26 (Pin 37)
  Play
  Record
  C
  D
  E
  F
